// Logisim project 2023-03-01.circ as structural Verilog: 1 circuit, main circuit main
module main (
  input  [3:0] in_1,
  input  enable0,
  input  clock,
  input  clear,
  input  select0,
  input  en_out,
  output [3:0] out_7
);

  wire not_1_out;
  wire [3:0] reg0_q, reg1_q;

  Register #(.width(4)) reg0 (.D(in_1), .en(enable0), .Q(reg0_q), .clk(clock), .clr(clear));
  not not_1 (not_1_out, enable0);
  Register #(.width(4)) reg1 (.D(in_1), .en(not_1_out), .Q(reg1_q), .clk(clock), .clr(clear));
  Multiplexer #(.width(4)) multiplexer_1 (.in0(reg0_q), .in1(reg1_q), .out(out_7), .sel(select0), .en(en_out));
endmodule
