// Logisim project 2023-03-15 atividade2.circ as structural Verilog: 1 circuit, main circuit main
module main (
  input  [3:0] dado,
  input  [1:0] \endereço ,
  input  select,
  input  clock,
  input  write_read,
  input  reset
);

  wire and_1_out, decoder_1_out0, decoder_1_out1, decoder_1_out2, decoder_1_out3;

  Decoder #(.select(2), .disabled(0)) decoder_1 (
    .out0(decoder_1_out0), .out1(decoder_1_out1), .out2(decoder_1_out2), .out3(decoder_1_out3),
    .sel(\endereço ), .en(and_1_out));
  Register #(.width(4)) \posição0  (.D(dado), .en(decoder_1_out0), .clk(clock), .clr(reset));  // open: Q
  Register #(.width(4)) \posição1  (.D(dado), .en(decoder_1_out1), .clk(clock), .clr(reset));  // open: Q
  and and_1 (and_1_out, select, ~write_read);  // AND_Gate
  Register #(.width(4)) \posição2  (.D(dado), .en(decoder_1_out2), .clk(clock), .clr(reset));  // open: Q
  Register #(.width(4), .trigger("falling")) \posição3  (
    .D(dado), .en(decoder_1_out3), .clk(clock), .clr(reset));  // open: Q
endmodule
