// Logisim project 2023-03-15.circ as structural Verilog: 1 circuit, main circuit main
// clock
module main (
  input  [3:0] in_1,
  input  [1:0] \endereço ,
  input  select,
  input  clock,
  input  write_read,
  input  reset,
  output [3:0] out_7
);

  RAM #(.addrWidth(2), .dataWidth(4)) ram_1 (
    .addr(\endereço ), .data(out_7), .sel(select), .clk(clock), .ld(write_read), .clr(reset));
endmodule
