// Logisim project Atividade_LaviniaBrandani08-03-23.circ as structural Verilog: 1 circuit, main circuit main
// reg2
module main (
  input  [3:0] entrada,
  input  _0_dado__1_int,
  input  clock,
  input  clear,
  output [3:0] saida
);

  wire and_1_out, and_2_out, and_3_out;
  wire [3:0] reg01_q, reg1_q, \reg_Instrução_q ;

  and and_1 (and_1_out, ~_0_dado__1_int, ~\reg_Instrução_q [1]);  // AND_Gate
  Register #(.width(4)) \reg_Instrução  (
    .D(entrada), .en(_0_dado__1_int), .Q(\reg_Instrução_q ), .clk(clock), .clr(clear));
  and and_2 (and_2_out, and_1_out, ~\reg_Instrução_q [0]);  // AND_Gate
  and and_3 (and_3_out, and_1_out, \reg_Instrução_q [0]);
  Register #(.width(4)) reg01 (.D(entrada), .en(and_3_out), .Q(reg01_q), .clk(clock), .clr(clear));
  Register #(.width(4)) reg1 (.D(entrada), .en(and_2_out), .Q(reg1_q), .clk(clock), .clr(clear));
  Multiplexer #(.width(4)) multiplexer_1 (
    .in0(reg1_q), .in1(reg01_q), .out(saida), .sel(\reg_Instrução_q [0]), .en(\reg_Instrução_q [1]));
endmodule
